# Fritzing sketch Circuit_Mina_Fina_Fatin_FyP (saved by Fritzing 0.9.3b)

parts:
  Part1 = Arduino Mega 2560 (Rev3)
  On_button = Round Pushbutton
  HC-SR04_Sensor_1 = HC-SR04 Ultrasonic Distance Sensor
  HC-SR04_Sensor_2 = HC-SR04 Ultrasonic Distance Sensor
  HC-SR04_Sensor_3 = HC-SR04 Ultrasonic Distance Sensor
  Water_pump = DC Motor
  AC_Motor = DC Motor
  J1 = Piezo Speaker
  J2 = Piezo Speaker
  Magnetic_Door_Switch = Reed switch [package=THT]
  LED3 = LED - 3mm [color="Red (633nm)" package="3 mm [THT]"]
  LED4 = LED - 3mm [color="Green (560nm)" package="3 mm [THT]"]
  LED5 = LED - 3mm [color="Red (633nm)" package="3 mm [THT]"]
  LED1 = LED - 3mm [color="Green (570nm)" package="3 mm [THT]"]
  LED6 = LED - 3mm [color="Yellow (595nm)" package="3 mm [THT]"]
  12V_Power_Supply = Power plug
  OMRON1 = OMRON PCB Power Relay – G5LE [part_number="G5LE-1\n" package=THT]
  AC_Power_Source = Power plug
  K1 = Relay [part_number=FRS1B-S package=THT]

nets:
  GND: Part1.GND, On_button.leg1, HC-SR04_Sensor_1.GND, HC-SR04_Sensor_2.GND, HC-SR04_Sensor_3.GND, J1.pin1, J2.pin1, LED3.cathode, LED4.cathode, LED1.cathode, LED6.cathode, 12V_Power_Supply.GND, K1.COIL2
  N1: Part1.D12_PWM, HC-SR04_Sensor_1.ECHO
  N2: Part1.D11_PWM, HC-SR04_Sensor_1.TRIG
  N3: Part1.D10_PWM, HC-SR04_Sensor_2.ECHO
  N4: Part1.D9_PWM, HC-SR04_Sensor_2.TRIG
  N5: Part1.D8_PWM, HC-SR04_Sensor_3.ECHO
  VIN: Part1.VIN, 12V_Power_Supply.VCC, OMRON1.C
  N6: Part1.D2_PWM, Magnetic_Door_Switch.pin_2
  N7: Part1.D3_PWM, On_button.leg0
  N8: Part1.D4_PWM, K1.COIL1
  N9: Part1.D5_PWM, J1.pin2
  N10: Part1.D6_PWM, J2.pin2
  N11: Part1.D7_PWM, HC-SR04_Sensor_3.TRIG
  VCC: Part1.5V, HC-SR04_Sensor_1.VCC, HC-SR04_Sensor_2.VCC, HC-SR04_Sensor_3.VCC
  N12: Part1.D22, LED3.anode
  N13: Part1.D23, LED6.anode
  N14: Part1.D24, LED1.anode
  N15: Part1.D25, LED5.anode
  N16: Part1.D26, LED4.anode
  N17: Part1.D27, OMRON1.COIL1
  N18: Water_pump.pin_2, OMRON1.B
  N19: AC_Motor.pin_1, K1.B
  N20: AC_Motor.pin_2, AC_Power_Source.GND
  N21: AC_Power_Source.VCC, K1.C1, K1.C2
