# Fritzing sketch Safwan_s_Schematic (saved by Fritzing 0.9.3b)
breadboards: 1

parts:
  Part1 = Arduino Nano (Rev3.0) (ICSP)
  IC1 = L293D [package=THT]
  IC2 = L293D [package=THT]
  IC3 = L293D [package=THT]
  IC4 = L293D [package=THT]
  M1 = Stepper Motor - Bipolar
  BAT1 = Battery Holders [package=battery-aa]
  U1 = SWITCH_SPDT [package=kps-1290]
  M2 = Stepper Motor - Bipolar
  M3 = Stepper Motor - Bipolar
  M4 = Stepper Motor - Bipolar

nets:
  N1: Part1.D2, IC3.In_3
  N2: Part1.D3, IC3.In_4
  N3: Part1.D4, IC3.In_1
  N4: Part1.D5, IC3.In_2
  N5: Part1.D6, IC1.In_2
  N6: Part1.D7, IC1.In_1
  N7: Part1.D8, IC1.In_4
  N8: Part1.D9, IC1.In_3
  N9: Part1.D10, IC4.In_1
  N10: Part1.GND, IC3.0V, BAT1.+
  N11: Part1.5V, U1.S
  N12: Part1.A3, IC2.In_3
  N13: Part1.A2, IC2.In_4
  N14: Part1.A1, IC2.In_2
  N15: Part1.A0, IC2.In_1
  N16: Part1.D12/MISO, IC4.In_4
  N17: Part1.D13/SCK, IC4.In_3
  N18: Part1.D11/MOSI, IC4.In_2
  N19: IC1.Enable_1, IC1.Enable_2, IC1.+V, IC2.Enable_1, IC2.+Vmotor, IC2.Enable_2, IC2.+V, IC3.Enable_1, IC3.+Vmotor, IC3.Enable_2, IC3.+V, IC4.Enable_1, IC4.+Vmotor, IC4.Enable_2, IC4.+V
  N20: IC1.Out_1_(_Controlled_by_Enable_1_), M3.C
  N21: IC1.0V, IC2.0V, IC4.0V
  N22: IC1.Out_2_(_Controlled_by_Enable_1_), M3.A
  N23: IC1.Out_3_(_Controlled_by_Enable_2_), M3.D
  N24: IC1.Out_4_(_Controlled_by_Enable_2_), M3.B
  N25: IC2.Out_1_(_Controlled_by_Enable_1_), M1.D
  N26: IC2.Out_2_(_Controlled_by_Enable_1_), M1.B
  N27: IC2.Out_3_(_Controlled_by_Enable_2_), M1.C
  N28: IC2.Out_4_(_Controlled_by_Enable_2_), M1.A
  N29: IC3.Out_1_(_Controlled_by_Enable_1_), M2.A
  N30: IC3.Out_2_(_Controlled_by_Enable_1_), M2.C
  N31: IC3.Out_3_(_Controlled_by_Enable_2_), M2.D
  N32: IC3.Out_4_(_Controlled_by_Enable_2_), M2.B
  N33: IC4.Out_1_(_Controlled_by_Enable_1_), M4.A
  N34: IC4.Out_2_(_Controlled_by_Enable_1_), M4.C
  N35: IC4.Out_3_(_Controlled_by_Enable_2_), M4.D
  N36: IC4.Out_4_(_Controlled_by_Enable_2_), M4.B
  N37: BAT1.-, U1.P
